# Fritzing sketch Scanbot Surfboard Scanner (saved by Fritzing 0.9.3b)
circuit board: 5.72956cm x 3.86108cm
breadboards: 1

parts:
  Q1 = NPN-Transistor [part_number=2N2222 package="TO92 [THT]"]
  R1 = Resistor [tolerance=±5% resistance=10k package=THT]
  R2 = Resistor [tolerance=±5% resistance=10k package=THT]
  U1 = CNZ1120 [part_number=H22A1 package=cnz1120]
  Q2 = NPN-Transistor [part_number=2N2222 package="TO92 [THT]"]
  R5 = Resistor [tolerance=±5% resistance=10k package=THT]
  R6 = Resistor [tolerance=±5% resistance=10k package=THT]
  S1 = Pushbutton [package=THT]
  R7 = Resistor [tolerance=±5% resistance=10k package=THT]
  LED1 = LED - 5mm [color="Red (633nm)" package="5 mm [THT]"]
  R8 = Resistor [tolerance=±5% resistance=220 package=THT]
  R3 = Resistor [tolerance=±5% resistance=220 package=THT]
  R4 = Resistor [tolerance=±5% resistance=10k package=THT]
  Gauge_Clock = female pin header, 1 pin [form="♀ (female)" part_number=clk]
  Pin_D5 = female pin header, 1 pin [form="♀ (female)" part_number=D5]
  Gauge_Data = female pin header, 1 pin [form="♀ (female)" part_number=data]
  Pin_D6 = female pin header, 1 pin [form="♀ (female)" part_number=D6]
  Gauge_Ground = female pin header, 1 pin [form="♀ (female)" part_number=gnd]
  Pin_D2 = female pin header, 1 pin [form="♀ (female)" part_number=D2]
  Pin_D9 = female pin header, 1 pin [form="♀ (female)" part_number=D9]
  Pin_D10 = female pin header, 1 pin [form="♀ (female)" part_number=D10]
  Pin_5v = female pin header, 1 pin [form="♀ (female)" part_number=5v]
  Pin_Gnd = female pin header, 1 pin [form="♀ (female)" part_number=Gnd]

nets:
  GND: Q1.E, U1.2, U1.4, Q2.E, R7.Pin_1, LED1.cathode, Gauge_Ground.pin1, Pin_Gnd.pin1
  N1: Q1.B, R1.Pin_0
  N2: Q1.C, R2.Pin_0, Pin_D6.pin1
  N3: R1.Pin_1, Gauge_Data.pin1
  5V: R2.Pin_1, R6.Pin_1, S1.leg1, R3.Pin_1, R4.Pin_0, Pin_5v.pin1
  N4: U1.1, R3.Pin_0
  N5: U1.3, R4.Pin_1, Pin_D2.pin1
  N6: Q2.B, R5.Pin_0
  N7: Q2.C, R6.Pin_0, Pin_D5.pin1
  N8: R5.Pin_1, Gauge_Clock.pin1
  N9: S1.leg0, R7.Pin_0, Pin_D9.pin1
  N10: LED1.anode, R8.Pin_1
  N11: R8.Pin_0, Pin_D10.pin1

notes:
  Indicator gauge voltage booster (1.5 to 5v)
  Controls
  Mouse optical encoder
